# Fritzing sketch buck (saved by Fritzing 0.9.6b)

parts:
  M1 = RioRand LM2596
  Mod1 = Raspberry Pi 4B
  Power_plug1 = Power plug

nets:
  N1: M1.Pin_1, Power_plug1.VCC
  N2: M1.Pin_2, Power_plug1.GND
  N3: M1.Pin_3, Mod1.5V
  N4: M1.Pin_4, Mod1.GND
