# Fritzing sketch cytron (saved by Fritzing 0.9.6b)

parts:
  Part1 = MDD10A
  U1 = ESP32-38PinWide [part_number=ESP32-38PinWide]
  Part2 = MDD10A
  M1 = DC Motor
  M2 = DC Motor
  M3 = DC Motor
  M4 = DC Motor
  Power_plug1 = Power plug
  Power_plug2 = Power plug

nets:
  N1: Part1.no_name_yet#connectorBatt-1, Power_plug1.VCC
  N2: Part1.no_name_yet#connectorBatt-2, Power_plug1.GND
  N3: Part1.no_name_yet#connectorM1A-1, M1.pin_1
  N4: Part1.no_name_yet#connectorM1B-1, M1.pin_2
  N5: Part1.no_name_yet#connectorM2A-1, M2.pin_2
  N6: Part1.no_name_yet#connectorM2B-1, M2.pin_1
  N7: Part1.no_name_yet#connectordir-1, U1.GPIO23
  N8: Part1.no_name_yet#connectordir-2, U1.GPIO17
  N9: Part1.no_name_yet#connectorgnd-1, U1.GND
  N10: Part1.no_name_yet#connectorpwm-1, U1.GPIO22
  N11: Part1.no_name_yet#connectorpwm-2, U1.GPIO16
  N12: U1.GPIO12, Part2.no_name_yet#connectordir-2
  N13: U1.GPIO13, Part2.no_name_yet#connectorpwm-2
  N14: U1.GPIO11, Part2.no_name_yet#connectorgnd-1
  N15: U1.GPIO19, Part2.no_name_yet#connectorpwm-1
  N16: U1.GPIO21, Part2.no_name_yet#connectordir-1
  N17: Part2.no_name_yet#connectorBatt-1, Power_plug2.VCC
  N18: Part2.no_name_yet#connectorBatt-2, Power_plug2.GND
  N19: Part2.no_name_yet#connectorM1A-1, M4.pin_1
  N20: Part2.no_name_yet#connectorM1B-1, M4.pin_2
  N21: Part2.no_name_yet#connectorM2A-1, M3.pin_2
  N22: Part2.no_name_yet#connectorM2B-1, M3.pin_1

custom parts:
  ESP32-38PinWide: Generic 38-Pin ESP32 with wide format (only access to one side of pins on a breadboard) based on Stephen Lilley's HiLetgo ESP-WROOM-32 ESP32 ESP-32S Development Board.
