# Fritzing sketch esp_raspi (saved by Fritzing 0.9.6b)

parts:
  Mod1 = Raspberry Pi 4B
  U1 = ESP32-38PinWide [part_number=ESP32-38PinWide]

nets:
  N1: Mod1.GPIO14, U1.GPIO9
  N2: Mod1.GPIO15, U1.GPIO10

custom parts:
  ESP32-38PinWide: Generic 38-Pin ESP32 with wide format (only access to one side of pins on a breadboard) based on Stephen Lilley's HiLetgo ESP-WROOM-32 ESP32 ESP-32S Development Board.
