# Fritzing sketch mpu (saved by Fritzing 0.9.6b)

parts:
  GY1 = MPU-6050 Board GY-521 [form="♀ (female)" package=THT]
  Mod1 = Raspberry Pi 4B

nets:
  N1: GY1.pin1, Mod1.5V
  N2: GY1.pin2, Mod1.GND
  N3: GY1.pin3, Mod1.GPIO3
  N4: GY1.pin4, Mod1.GPIO2

custom parts:
  MPU-6050 Board GY-521: Acelerometro y Giroscopio MPU-6050 Board GY-521
