# Fritzing sketch servo (saved by Fritzing 0.9.6b)

parts:
  Mod1 = Raspberry Pi 4B
  Part1 = 16-Channel 12-bit PWM Servo Shield - I2C [part_number=1411]
  Power_plug1 = Power plug
  J1 = Basic Servo
  J2 = Basic Servo
  J3 = Basic Servo
  J4 = Basic Servo
  J5 = Basic Servo

nets:
  N1: Mod1.GPIO2, Part1.SDA
  N2: Mod1.GPIO3, Part1.SCL
  GND: Mod1.GND, Part1.GND, Power_plug1.GND, J1.gnd, J2.gnd, J3.gnd, J4.gnd, J5.gnd
  N3: Part1.PWRIN, Power_plug1.VCC
  N4: Part1.PWM7, J3.pulse
  VCC: Part1.5.0V, J1.vcc, J2.vcc, J3.vcc, J4.vcc, J5.vcc
  N5: Part1.PWM5, J4.pulse
  N6: Part1.PWM2, J5.pulse
  N7: Part1.PWM14, J1.pulse
  N8: Part1.PWM11, J2.pulse

custom parts:
  16-Channel 12-bit PWM Servo Shield - I2C: You want to make a cool Arduino robot, maybe a hexapod walker, or maybe just a piece of art with a lot of moving parts. Or maybe you want to drive a lot of LEDs with precise PWM output. This shield is just like our popular PWM/Servo Breakout but now Arduino-ready and works with any Arduino that uses shields: Uno, Leo, Mega, ADK, its all good. Using only two I2C pins, control 16 free-running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
