# Fritzing sketch tf_luna (saved by Fritzing 0.9.6b)

parts:
  A1 = tf-luna lidar
  Mod1 = Raspberry Pi 4B

nets:
  N1: A1.Pin_1, Mod1.5V
  N2: A1.Pin_2, Mod1.GPIO8
  N3: A1.Pin_3, Mod1.GPIO9
  N4: A1.Pin_4, Mod1.GND

custom parts:
  tf-luna lidar: TF-Luna is using Time of Flight (TOF) principle to measure distance, and it periodically emits near infrared modulated wave.
